# Fritzing sketch schamatic (saved by Fritzing 0.9.2b)
circuit board: 5.23457cm x 2.94268cm
breadboards: 1

parts:
  J5 = female pin header, 2 pins [form="♀ (female)"]
  D1 = Rectifier Diode [part_number=1N4001 package="300 mil [THT]"]
  R14 = Resistor [tolerance=±10% resistance=8.2k package=THT]
  R13 = Resistor [tolerance=±10% resistance=33k package=THT]
  R16 = Resistor [tolerance=±10% resistance=10k package=THT]
  R11 = Resistor [tolerance=±10% resistance=100k package=THT]
  J3 = female pin header, 3 pins [form="♀ (female)"]
  J4 = female pin header, 2 pins [form="♀ (female)"]
  R7 = Resistor [tolerance=±10% resistance=10k package=THT]
  Q3 = TRANSISTOR_NPN [package=to-92-ammo]
  Q2 = TRANSISTOR_NPN [package=to-92-ammo]
  J2 = female pin header, 2 pins [form="♀ (female)"]
  R12 = Resistor [tolerance=±10% resistance=33k package=THT]
  U2 = ESP8266 WiFi Module [part_number=ESP8266]
  Q1 = TRANSISTOR_NPN [package=to-92-ammo]
  J6 = female pin header, 1 pin [form="♀ (female)"]

nets:
  N1: J5.pin1, U2.RXD
  N2: J5.pin2, U2.TXD
  N3: D1.cathode, U2.CH_PD, Q1.E
  N4: D1.anode, R16.Pin_1, Q2.E, U2.GPIO_13
  N5: R14.Pin_0, R16.Pin_0, R11.Pin_0, J3.pin1, J4.pin2, R7.Pin_0, Q3.E, U2.GND
  N6: R14.Pin_1, Q3.B, R12.Pin_0
  N7: R13.Pin_0, Q3.C, Q2.B
  N8: R13.Pin_1, J3.pin3, J4.pin1, R12.Pin_1
  N9: R11.Pin_1, J2.pin1, Q1.B
  N10: J3.pin2, Q2.C, J2.pin2, U2.VCC, Q1.C
  N11: R7.Pin_1, U2.GPIO_15
  N12: U2.GPIO_0, J6.pin1
  N13: U2.GPIO_16, U2.REST

custom parts:
  ESP8266 WiFi Module: Generic WiFi Module based on the ESP8266 with onboard PCB antenna and UART communications
